# Fritzing sketch EQDirect_MCP2221 (saved by Fritzing 0.9.10b)
circuit board: 8.46667cm x 5.64444cm
breadboards: 1

parts:
  U1 = MCP2221 [package="DIP14 [THT]"]
  U2 = RJ45 Jack [package=rj45-8]
  CONN1 = USB connector [package=THT]

nets:
  VDD: U1.VDD, CONN1.5V
  N1: U1.URx, U2.5
  N2: U1.UTx, U2.6
  N3: U1.D-, CONN1.d-
  N4: U1.D+, CONN1.d+
  VSS: U1.Vss, U2.4, CONN1.GND, CONN1.chassis5, CONN1.chassis6

custom parts:
  MCP2221: USB to I2C/UART converter with GPIO
