# Fritzing sketch Schematic (saved by Fritzing 0.9.10b)
breadboards: 1

parts:
  Mod1 = OLED Mono 0.56 inch blue or white
  U2 = RELAY [package=relay-t9a-2]
  U3 = LIPO-2000mAh [package=lipo-2000]
  ChargePort = Camdenboss CTB0158-2 [part_number=CTB0158-2 package=THT]
  M1 = INA3221 Triple Channel Current/Voltage Monitor Module [part_number="3221 Black"]
  Q1 = Basic FET N-Channel [package="DPak [SMD]"]
  R1 = Resistor [tolerance=±5% power=0.25 resistance=10k package=THT]
  D1 = Zener Diode [part_number=30SQ050 breakdown_voltage=3.6V package="300 mil [THT]"]
  U4 = RELAY [package=relay-t9a-2]
  U5 = RELAY [package=relay-t9a-2]
  R2 = Resistor [tolerance=±5% power=0.25 resistance=2k package=THT]
  Heater1 = Camdenboss CTB0158-2 [part_number=CTB0158-2 package=THT]
  D2 = Zener Diode [part_number=30SQ050 breakdown_voltage=3.6V package="300 mil [THT]"]
  D3 = Zener Diode [part_number=30SQ050 breakdown_voltage=3.6V package="300 mil [THT]"]
  Heater2 = Camdenboss CTB0158-2 [part_number=CTB0158-2 package=THT]
  Q2 = Basic FET N-Channel [package="DPak [SMD]"]
  R3 = Resistor [tolerance=±5% power=0.25 resistance=10k package=THT]
  R4 = Resistor [tolerance=±5% power=0.25 resistance=2k package=THT]
  M2 = RioRand LM2596 [part_number=3.3V/2A]
  S1 = Round Pushbutton
  C1 = Capacitor [part_number=100nF package=cap-pth-small-kit]
  DC2 = DC_DC_XL4016 [part_number=19V package=board_screw]
  R5 = Resistor [tolerance=±5% power=0.25 resistance=10k package=THT]
  LED1 = LED - 5mm [color="Red (633nm)" current=0.030 package="5 mm [THT]"]
  Q3 = TRANSISTOR_NPN [package=to-92-ammo]
  R6 = Resistor [tolerance=±5% power=0.25 resistance=470 package=THT]
  R7 = Resistor [tolerance=±5% power=0.25 resistance=10k package=THT]
  U6 = NodeMCU V1.0
  M3 = RioRand LM2596 [part_number=8V/2A]
  ImagingCam = Camdenboss CTB0158-2 [part_number=CTB0158-2 package=THT]
  R9 = Resistor [tolerance=±5% power=0.25 resistance=10k package=THT]
  D4 = Zener Diode [part_number=30SQ050 breakdown_voltage=3.6V package="300 mil [THT]"]
  A1 = DHT22 module
  D5 = Zener Diode [part_number=30SQ050 breakdown_voltage=3.6V package="300 mil [THT]"]
  PC = Camdenboss CTB0158-2 [part_number=CTB0158-2 package=THT]
  M4 = INA3221 Triple Channel Current/Voltage Monitor Module [part_number="3221 Black"]
  Mount = Camdenboss CTB0158-2 [part_number=CTB0158-2 package=THT]
  F1 = FUSE [part_number=1.5A package=fuse_5mm]
  F2 = FUSE [part_number=2.5A package=fuse_5mm]
  F3 = FUSE [part_number=2.5A package=fuse_5mm]
  F4 = FUSE [part_number=1A package=fuse_5mm]
  Q5 = Basic FET P-Channel [part_number=IRF9622 package="DPak [SMD]"]
  Q6 = TRANSISTOR_NPN [package=to-92-ammo]
  R10 = Resistor [tolerance=±5% power=0.25 resistance=10k package=THT]

nets:
  N1: Mod1.SDA, M1.SCL, U6.D2, M4.SCL
  N2: Mod1.SCL, M1.SDA, U6.D1, M4.SDA
  VCC: Mod1.VCC, M1.VS, M2.Pin_3, R5.Pin_0, U6.3V3, A1.VCC
  GND: Mod1.GND, U6.GND, A1.GND
  N3: U2.COIL1, Mount.pin2
  !MountPower: U2.COIL2, U6.SD0
  N4: U2.MAIN, F1.2
  N5: U2.NC, Mount.pin1
  N6: U3.+, M1.VPU, M1.VN1-, M2.Pin_1, R6.Pin_0, M4.VPU
  GND_2: U3.-, U5.COIL1
  GND_3: ChargePort.pin1, M1.GND, Q1.source, R1.Pin_1, U4.COIL2, Q2.source, R3.Pin_1, M2.Pin_2, M2.Pin_4, S1.leg0, C1.2, DC2.IN-, DC2.OUT-, Q3.E, M3.Pin_2, PC.pin2, M4.GND, Q6.E
  N7: ChargePort.pin2, D1.anode
  N8: M1.VN3+, M1.VN2+, U5.NO, R9.Pin_0, M4.VN3+, M4.VN2+, M4.VN1+
  N9: M1.VN3-, F3.1
  N10: M1.VN2-, F2.1
  12.8V: M1.VN1+, U4.NC, U5.MAIN
  N11: Q1.Gate, R1.Pin_0, R2.Pin_1
  N12: Q1.drain, Heater1.pin2
  N13: D1.cathode, U4.MAIN
  N14: U4.COIL1, U6.CMD
  N15: U5.COIL2, U6.SD1
  HeaterPWM1: R2.Pin_0, U6.SD3
  N16: Heater1.pin1, D2.cathode
  N17: D2.anode, F2.2
  N18: D3.cathode, Heater2.pin1
  N19: D3.anode, F3.2
  N20: Heater2.pin2, Q2.drain
  N21: Q2.Gate, R3.Pin_0, R4.Pin_1
  HeaterPWM2: R4.Pin_0, U6.SD2
  N22: S1.leg1, C1.1, R5.Pin_1, U6.D7
  N23: DC2.IN+, M4.VN1-
  N24: DC2.OUT+, D5.anode
  N25: LED1.cathode, Q3.C
  N26: LED1.anode, R6.Pin_1
  N27: Q3.B, R7.Pin_0
  N28: R7.Pin_1, U6.D3
  N29: U6.D0, U6.RST
  N30: U6.D5, A1.DAT
  N31: U6.D6, R10.Pin_1
  N32: M3.Pin_1, F4.2
  N33: M3.Pin_3, D4.anode
  N34: M3.Pin_4, ImagingCam.pin2
  N35: ImagingCam.pin1, D4.cathode
  N36: R9.Pin_1, Q5.Gate, Q6.C
  N37: D5.cathode, PC.pin1
  N38: M4.VN3-, Q5.source
  N39: M4.VN2-, F1.1
  N40: F4.1, Q5.drain
  N41: Q6.B, R10.Pin_0

notes:
  AstroPhotoPowerBox, 1.1

custom parts:
  OLED Mono 0.56 inch blue or white: OLED, I2C 3.3V - 5V Blue and White text versions
  INA3221 Triple Channel Current/Voltage Monitor Module: INA3221 Triple Channel Current/Voltage Monitor Module Links: INA3221 product information
  NodeMCU V1.0: ESP8266 based NodeMCU
  DHT22 module: DHT22 module. Pins GND VCC Data.
